# Fritzing sketch CPC-power-source (saved by Fritzing 0.9.3b)

parts:
  OUT = COMPUTER-PERIPHERAL-POWER [package=computer-peripheral-power-ra]
  USB = USB Connectors [package=usb-microb]
  D7 = Rectifier Diode 10A [part_number=P1000K]
  D8 = Rectifier Diode 10A [part_number=P1000K]
  D10 = Rectifier Diode 10A [part_number=P1000K]
  D9 = Rectifier Diode 10A [part_number=P1000K]
  CPC_5V = Header 2 [package=screwterminal-3.5mm-2_lock]
  CPC_12V_(center_is_-) = Power Jack [package=power_jack_slot]
  3_5"_Floppy = Header 4 [package=molex-1x4_lock]
  IN = COMPUTER-PERIPHERAL-POWER [package=computer-peripheral-power-ra]
  S1 = SPST Switch [package=switch-spdt_kit]
  R1 = Resistor [tolerance=±5% resistance=220 package=THT]
  D5 = Rectifier Diode 10A [part_number=P1000K]
  D6 = Rectifier Diode 10A [part_number=P1000K]
  R2 = Trimmer Potentiometer [maximum_resistance=10kΩ package=THT]
  LCD1 = LCD screen
  5V_AM = ACS712 Low Current Sensor Board v12
  12V_AM = ACS712 Low Current Sensor Board v12
  ProMini = Arduino Pro Mini (5V)

nets:
  5V: OUT.5V, CPC_5V.1, 3_5"_Floppy.1, S1.P, R1.Pin_1, LCD1.VDD, 5V_AM.IP-, 5V_AM.5V, 12V_AM.5V, ProMini.VCC
  N1: OUT.12V, 12V_AM.IP-
  GND: OUT.GND, D7.anode, D10.anode, CPC_5V.2, 3_5"_Floppy.2, R2.leg1, LCD1.VSS, LCD1.R/W, LCD1.LED-, 5V_AM.GND, ProMini.GND
  N2: OUT.NC, IN.NC, D5.cathode, 12V_AM.GND
  N3: USB.GND, D10.cathode
  N4: USB.VBUS, D9.anode
  N5: D7.cathode, IN.GND
  N6: D8.cathode, D9.cathode, 5V_AM.IP+
  N7: D8.anode, IN.5V
  N8: CPC_12V_(center_is_-).GNDBREAK, CPC_12V_(center_is_-).GND, D6.cathode
  N9: CPC_12V_(center_is_-).PWR, D5.anode
  N10: IN.12V, D6.anode, 12V_AM.IP+
  N11: S1.O, R2.leg2
  N12: R1.Pin_0, LCD1.LED+
  N13: R2.wiper, LCD1.V0
  N14: LCD1.RS, ProMini.D10
  N15: LCD1.E, ProMini.D9
  N16: LCD1.DB4, ProMini.D2
  N17: LCD1.DB5, ProMini.D3
  N18: LCD1.DB6, ProMini.D4
  N19: LCD1.DB7, ProMini.D5
  N20: 5V_AM.VO, ProMini.A1
  N21: 12V_AM.VO, ProMini.A0
